# Fritzing sketch Circuit Diagram (saved by Fritzing 0.9.3b)

parts:
  Part1 = Arduino Uno (Rev3)
  part = Resistor [tolerance=±5% resistance=20k package=THT]
  I2C_LCD = LCD-16X2 [package=lcd-16x2_noholes]  # not connected
  IC1 = IC, SIP package, 16 pins [chip_label="I2C LCD Backpack"]  # not connected
  IC2 = IC, SIP package, 4 pins
  IR_SENSOR = smd LED [color="Infrared (940nm)" package="0805 [SMD]"]
  Transmitter = smd LED [color="Orange (605nm)" package="0805 [SMD]"]
  part_2 = Resistor [tolerance=±5% resistance=100 package=THT]
  Servo_9G = Dagu DGServo 9g (Top view) [part_number=RS001B]
  BAT1 = BC9VPC [package=bc9vpc]  # not connected

nets:
  N1: Part1.A4/SDA, IC2.pin2
  N2: Part1.A5/SCL, IC2.pin1
  N3: Part1.D13/SCK, part.Pin_0, Transmitter.anode
  N4: Part1.D5_PWM, Servo_9G.pulse
  5V: Part1.5V, Servo_9G.vcc
  N5: part.Pin_1, part_2.Pin_1
  N6: IR_SENSOR.cathode, part_2.Pin_0
  N7: IR_SENSOR.anode, Transmitter.cathode
